# Fritzing sketch robotling2_v4 (saved by Fritzing 0.9.9b)
circuit board: 7cm x 3.8cm
breadboards: 2

parts:
  Mod1 = Raspberry Pi Pico  # not connected
  M2 = male pin header, 3 pins [form="♂ (male)"]
  J2 = male pin header, 3 pins [form="♂ (male)"]
  M1 = male pin header, 3 pins [form="♂ (male)"]
  M3 = male pin header, 3 pins [form="♂ (male)"]
  J2_2 = female pin header, 3 pins [form="♀ (female)"]
  S1 = SPST Switch [package=switch-spdt_lock.007s]
  Q1 = PNP-Transistor [package="SOT-23 [SMD]"]
  J5 = female pin header, 20 pins [form="♀ (female)"]
  J6 = female pin header, 20 pins [form="♀ (female)"]
  J1 = male pin header, 2 pins [form="♂ (male)"]
  Ai0/1 = male pin header, 3 pins [form="♂ (male)"]
  Ai1 = male pin header, 3 pins [form="♂ (male)"]
  D0/Ai2 = male pin header, 3 pins [form="♂ (male)"]
  R1 = Resistor [tolerance=±5% resistance=1k power=0.25 package=THT]
  R2 = Resistor [tolerance=±5% resistance=1.5k power=0.25 package=THT]
  R3 = Resistor [tolerance=±5% resistance=1k power=0.25 package=THT]
  R4 = Resistor [tolerance=±5% resistance=1k power=0.25 package=THT]
  R5 = Resistor [tolerance=±5% resistance=1.5k power=0.25 package=THT]
  R6 = Resistor [tolerance=±5% resistance=1.5k power=0.25 package=THT]
  I2C = male pin header, 4 pins [form="♂ (male)"]
  R7 = Resistor [tolerance=±5% power=0.25 resistance=8.2k package=THT]
  R8 = Resistor [tolerance=±5% power=0.25 resistance=8.2k package=THT]
  S2 = Momentary Switch [package=ksa_sealed_tac_switch]
  R9 = Resistor [tolerance=±5% power=0.25 resistance=220 package=THT]
  LED1 = LED - 3mm [color="Yellow (595nm)" current=0.030 package="3 mm [THT]"]
  I2C1 = male pin header, 4 pins [form="♂ (male)"]
  I2C2 = Header 4 [package=1x04-1mm-ra]
  J3 = male pin header, 3 pins [form="♂ (male)"]
  J4 = male pin header, 3 pins [form="♂ (male)"]

nets:
  N1: M2.pin1, J2.pin1, M1.pin1, M3.pin1, J2_2.pin2, J6.pin18, J1.pin1, Ai0/1.pin1, Ai1.pin1, D0/Ai2.pin1, R2.Pin_1, R5.Pin_1, R6.Pin_1, I2C.pin1, LED1.cathode, I2C1.pin1, I2C2.1, J4.pin1
  N2: M2.pin2, J2.pin2, M1.pin2, M3.pin2, J2_2.pin3, Ai0/1.pin2, Ai1.pin2, D0/Ai2.pin2, J3.pin3, J4.pin2
  N3: M2.pin3, J5.pin17
  N4: J2.pin3, J5.pin16
  N5: M1.pin3, J5.pin7
  N6: M3.pin3, J6.pin7
  N7: J2_2.pin1, S1.P, J3.pin1
  N8: S1.S, J1.pin2
  N9: Q1.2, J6.pin19
  N10: Q1.0, J6.pin20
  N11: Q1.1, J3.pin2
  N12: J5.pin6, R9.Pin_1
  N13: J5.pin9, J4.pin3
  N14: J5.pin14, I2C1.pin3
  N15: J5.pin15, I2C1.pin4
  N16: J5.pin19, I2C.pin3, R8.Pin_0, I2C2.4
  N17: J5.pin20, I2C.pin4, R7.Pin_0, I2C2.3
  N18: J6.pin3, S2.3
  N19: J6.pin9, I2C1.pin2
  N20: J6.pin10, S2.1
  N21: J6.pin11, R1.Pin_0, R2.Pin_0
  N22: J6.pin12, R3.Pin_0, R5.Pin_0
  N23: J6.pin14, R4.Pin_0, R6.Pin_0
  N24: J6.pin16, I2C.pin2, R7.Pin_1, R8.Pin_1, I2C2.2
  N25: Ai0/1.pin3, R1.Pin_1
  N26: Ai1.pin3, R3.Pin_1
  N27: D0/Ai2.pin3, R4.Pin_1
  N28: R9.Pin_0, LED1.anode

notes:
  D
  off
  (+)(-)
  VB
  VS
  gd
  17cs
  21
  27
  3V
  3Vn
  Arf
  28
  26
  22
  run
  20en
  19mo
  18sc
  16dc
  15y
  14x
  10
  12a
  11
  13b
  8b
  6r
  7g
  9
  3
  4
  2
  5
  0
  1
  OFF
  5V
  D1/3V
  tx/sd
  rx/sc
  Robotling2-pico v0.4
  (c) 2021 T. Euler
  D2

custom parts:
  Raspberry Pi Pico: Raspberry Pi Pico. Based around the RP2040 microcontroller the Pico is a low cost microcontroller device bringing Raspberry Pi quality, cost, and easy of use to the microcontroller space. Jan 2021, Split part in to two versions: tht (this one) and SMD. This one will drill holes for a .1 in header in pcb to allow plugging in the module as well as providing pads to solder the module to the top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
